# Fritzing sketch fritzing (saved by Fritzing 0.8.7b)
breadboards: 1

parts:
  Part1 = Adafruit Feather 32u4 Basic Proto [part_number="Adafruit #2771"]
  Part2 = Adafruit LSM9DS1 9DoF Breakout [part_number="Adafruit #3387"]
  BATT1 = LiPoly Battery (1300mAh)  # not connected
  S1 = Toggle Switch [package=THT]
  SP1 = SPEAKER [package=pcb_mount_speaker]

nets:
  GND: Part1.GND, Part2.GND, S1.L2, SP1.+
  N1: Part1.A0, SP1.-
  +3V3: Part1.+3V3, Part2.VIN, S1.L1
  N2: Part1.13, S1.COM
  N3: Part1.3, Part2.SCL
  N4: Part1.2, Part2.SDA

custom parts:
  Adafruit Feather 32u4 Basic Proto: At the Feather 32u4's heart is at ATmega32u4 clocked at 8 MHz and at 3.3V logic, a chip setup we've had tons of experience with as it's the same as the Flora. This chip has 32K of flash and 2K of RAM, with built in USB so not only does it have a USB-to-Serial program & debug capability built in with no need for an FTDI-like chip, it can also act like a mouse, keyboard, USB MIDI device, etc.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
  Adafruit LSM9DS1 9DoF Breakout: Add motion, direction and orientation sensing to your Arduino project with this all-in-one 9-DOF sensor. Inside the chip are three sensors, one is a classic 3-axis accelerometer, which can tell you which direction is down towards the Earth (by measuring gravity) or how fast the board is accelerating in 3D space. The other is a 3-axis magnetometer that can sense where the strongest magnetic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
  LiPoly Battery (1300mAh): Lithium Ion Polymer Battery (1300mAh)
